// Logisim project bots.circ as structural Verilog: 1 circuit, main circuit main
module main (
  input  CURR_PLAYER,
  input  PREP_PHASE_END,
  input  CLR,
  input  CLK,
  input  WIN,
  input  [3:0] SHIPS_NUMBER,
  output [3:0] X,
  output [3:0] Y,
  output ROTATED,
  output CONFIRM
);

  wire _10SHIPS, and_1_out, BOOT_PHASE, not_1_out, not_3_out, or_1_out, or_2_out, SHOOT_PHASE, SHOT_DONE;

  Clock clock_1 ();  // open: out
  not not_1 (not_1_out, PREP_PHASE_END);
  not not_2 (not_1_out, PREP_PHASE_END);
  not not_3 (not_3_out, _10SHIPS);
  and and_1 (and_1_out, CURR_PLAYER, ~BOOT_PHASE, PREP_PHASE_END, ~WIN);  // AND_Gate
  and and_2 (BOOT_PHASE, not_1_out, not_3_out);
  or or_1 (or_1_out, and_1_out, or_2_out);
  or or_2 (or_2_out, SHOT_DONE, WIN);
  S_R_Flip_Flop s_r_ff_1 (.S(and_1_out), .clk(or_1_out), .R(or_2_out), .Q(SHOOT_PHASE));  // open: Qn, preset, reset, en
  map_generator_main main_1 (
    .BOOT_PHASE(BOOT_PHASE), .CLK(CLK), .SHIPS_NUMBER(SHIPS_NUMBER), .out_5(X), .out_6(Y), .ROTATED(ROTATED),
    .out_8(CONFIRM), .out_9(_10SHIPS), .in_1(CLR));
  bot_0_main main_2 (
    .in_1(CLK), .in_2(SHOOT_PHASE), .in_3(SHOOT_PHASE), .CONFIRM(CONFIRM), .X(X), .Y(Y), .out_7(SHOT_DONE),
    .in_4(CLR));
  Pull_Resistor pull_resistor_1 (.node(X));
  Pull_Resistor pull_resistor_2 (.node(Y));
  Pull_Resistor pull_resistor_3 (.node(ROTATED));
  Pull_Resistor pull_resistor_4 (.node(CONFIRM));

  // Other names for the same wires on the sheet: CONFIRM_CLOCK = CONFIRM; ROTATION_CLOCK = ROTATED;
  //   SHIP_NUMBER[3:0] = SHIPS_NUMBER
endmodule
